# Fritzing sketch serverPumpCirtuit (saved by Fritzing 1.0.2b)
breadboards: 1

parts:
  Mod1 = Raspberry Pi 4B
  Q1 = MOSFET-NCHANNEL [package=to220v]
  LED1 = LED - 3mm [color="Red (633nm)" current=0.030A package="3 mm [THT]"]  # not connected
  R1 = Resistor [tolerance=±5% resistance=220 package="2512 [SMD]"]
  M1 = DC Motor [voltage_(max)=6V voltage_(min)=3V]

nets:
  N1: Mod1.GPIO2, Q1.G
  N2: Mod1.5V, M1.pin_2
  N3: Mod1.GPIO3, R1.Pin_0
  N4: Mod1.GND, Q1.S
  N5: Q1.D, M1.pin_1
